# Fritzing sketch Arduino_serial_4066_uno (saved by Fritzing 1.0.0d)
breadboards: 1

parts:
  Composant2 = Arduino Mega ADK (Rev3)
  IC1 = IC, DIP package, 14 pins [chip_label=CD4066BE]

nets:
  N1: Composant2.D19/RX1, IC1.pin2, IC1.pin4
  N2: Composant2.D18/TX1, IC1.pin9, IC1.pin11
  N3: Composant2.5V, IC1.pin14
  N4: Composant2.D2_PWM, IC1.pin6
  N5: Composant2.D3_PWM, IC1.pin12

notes:
  0x08
  [13]
  0x0A
  [5]
  LED
  [1]
  BTN
  [10]
  [8]
  [3]
